# Fritzing sketch sketsa_straight_cable_WIFI (saved by Fritzing 0.9.10b)
breadboards: 1

parts:
  NodeMCU_v1 = NodeMCU v3 LoLin [part_number=ESP8266]
  DHT1 = DHT22 Humidity and Temperature Sensor
  Grove1 = Grove Dust Sensor
  F1 = Fan - Ventilador [package=THT]
  YwRobot_Power_Supply1 = YwRobot Breadboard Power Supply [part_number=545043]
  D1 = Rectifier Diode [part_number=1N4001 package="300 mil [THT]"]

nets:
  N1: NodeMCU_v1.D5, Grove1.SIG
  N2: NodeMCU_v1.D6, Grove1.NC
  N3: NodeMCU_v1.D7, DHT1.DATA
  GND: NodeMCU_v1.GND, DHT1.GND, Grove1.GND, YwRobot_Power_Supply1.GND#13
  3V3: NodeMCU_v1.3V3, DHT1.VDD
  VIN: NodeMCU_v1.VIN, Grove1.VCC, YwRobot_Power_Supply1.VCC#9
  N4: F1.5V, YwRobot_Power_Supply1.VCC#5, D1.anode
  N5: F1.GND, YwRobot_Power_Supply1.GND#11, D1.cathode

custom parts:
  NodeMCU v3 LoLin: NodeMCU v3 LoLin NodeMCU (http://www.nodemcu.com/) is an open source IoT platform. It includes firmware (https://nodemcu-build.com/) which runs on the ESP8266 Wi-Fi SoC from Espressif Systems, and hardware which is based on the ESP-12E module. The term "NodeMCU" by default refers to the firmware rather than the dev kits. The firmware uses the Lua scripting language. It is based on the eLua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
  Grove Dust Sensor: PPD42 Grove Dust Sensor
  Fan - Ventilador: Ventilador de 2 pines, se encuentra comunmente en computadoras de escritorio
  YwRobot Breadboard Power Supply: The YwRobot Breadboard Power Supply (MB-V2) has two power rails; they can be 5V or 3V3. Power to the module can be provided through the female USB socket or through the A10 (female) 2.1mm power jack.
